# Fritzing sketch Pico PyDeck (saved by Fritzing 0.9.3b)
breadboards: 1

parts:
  Mod1 = Raspberry Pi Pico
  S1 = Pushbutton [package="[THT]"]
  S2 = Pushbutton [package="[THT]"]
  S3 = Pushbutton [package="[THT]"]
  S4 = Pushbutton [package="[THT]"]
  S5 = Pushbutton [package="[THT]"]
  S6 = Pushbutton [package="[THT]"]
  S7 = Pushbutton [package="[THT]"]
  S8 = Pushbutton [package="[THT]"]
  S9 = Pushbutton [package="[THT]"]
  S10 = Pushbutton [package="[THT]"]
  R1 = Resistor [tolerance=±5% resistance=220 package=THT]
  R2 = Resistor [tolerance=±5% resistance=220 package=THT]
  R3 = Resistor [tolerance=±5% resistance=220 package=THT]
  R4 = Resistor [tolerance=±5% resistance=220 package=THT]
  R5 = Resistor [tolerance=±5% resistance=220 package=THT]
  R6 = Resistor [tolerance=±5% resistance=220 package=THT]
  R7 = Resistor [tolerance=±5% resistance=220 package=THT]
  R8 = Resistor [tolerance=±5% resistance=220 package=THT]
  R9 = Resistor [tolerance=±5% resistance=220 package=THT]
  LED2 = LED - 5mm [color="Red (633nm)" package="5 mm [THT]"]
  LED3 = LED - 5mm [color="Red (633nm)" package="5 mm [THT]"]
  LED4 = LED - 5mm [color="Red (633nm)" package="5 mm [THT]"]
  LED5 = LED - 5mm [color="Red (633nm)" package="5 mm [THT]"]
  LED6 = LED - 5mm [color="Red (633nm)" package="5 mm [THT]"]
  LED7 = LED - 5mm [color="Red (633nm)" package="5 mm [THT]"]
  LED8 = LED - 5mm [color="Red (633nm)" package="5 mm [THT]"]
  LED9 = LED - 5mm [color="Red (633nm)" package="5 mm [THT]"]
  LED10 = LED - 5mm [color="Red (633nm)" package="5 mm [THT]"]
  LED11 = LED - 5mm [color="Red (633nm)" package="5 mm [THT]"]
  R10 = Resistor [tolerance=±5% resistance=220 package=THT]
  U1 = ENCODER-QUADRATURE [package=encoder-16mm-quad]

nets:
  N1: Mod1.pin_1, S1.Pin_3
  N2: Mod1.pin_2, S2.Pin_3
  N3: Mod1.pin_3, Mod1.pin_8, Mod1.pin_13, Mod1.pin_18, Mod1.pin_23, Mod1.pin_28, Mod1.pin_33, Mod1.pin_38, Mod1.pin_42, S1.Pin_1, S1.Pin_2, S2.Pin_2, S3.Pin_2, S4.Pin_2, S5.Pin_2, S6.Pin_2, S7.Pin_2, S8.Pin_2, S9.Pin_1, S9.Pin_2, S10.Pin_2, R7.Pin_0, LED2.cathode, LED3.cathode, LED4.cathode, LED5.cathode, LED6.cathode, LED7.cathode, LED8.cathode, LED9.cathode, LED10.cathode, LED11.cathode, U1.A
  N4: Mod1.pin_4, S3.Pin_3
  N5: Mod1.pin_5, S4.Pin_3
  N6: Mod1.pin_6, S5.Pin_3, S5.Pin_4
  N7: Mod1.pin_7, S6.Pin_3, S6.Pin_4
  N8: Mod1.pin_9, S7.Pin_3, S7.Pin_4
  N9: Mod1.pin_10, S8.Pin_3, S8.Pin_4
  N10: Mod1.pin_11, S9.Pin_3, S9.Pin_4
  N11: Mod1.pin_12, S10.Pin_3, S10.Pin_4
  N12: Mod1.pin_15, R1.Pin_0
  N13: Mod1.pin_16, R2.Pin_0
  N14: Mod1.pin_17, R3.Pin_0
  N15: Mod1.pin_19, R4.Pin_0
  N16: Mod1.pin_21, R5.Pin_0
  N17: Mod1.pin_22, R6.Pin_0
  N18: Mod1.pin_24, R8.Pin_0
  N19: Mod1.pin_25, R9.Pin_0
  N20: Mod1.pin_26, R10.Pin_0
  N21: Mod1.pin_31, U1.B
  N22: Mod1.pin_36, U1.C
  N23: R1.Pin_1, LED2.anode
  N24: R2.Pin_1, LED3.anode
  N25: R3.Pin_1, LED4.anode
  N26: R4.Pin_1, LED5.anode
  N27: R5.Pin_1, LED6.anode
  N28: R6.Pin_1, LED7.anode
  N29: R7.Pin_1, LED8.anode
  N30: R8.Pin_1, LED9.anode
  N31: R9.Pin_1, LED10.anode
  N32: LED11.anode, R10.Pin_1

custom parts:
  Raspberry Pi Pico: Raspberry Pi Pico. Based around the RP2040 microcontroller the Pico is a low cost microcontroller device bringing Raspberry Pi quality, cost, and easy of use to the microcontroller space. Jan 2021, Split part in to two versions: tht (this one) and SMD. This one will drill holes for a .1 in header in pcb to allow plugging in the module as well as providing pads to solder the module to the top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
